// Logisim project Circuito Calculadora.circ as structural Verilog: 2 circuits, main circuit main
module main (
);

  wire sumador_completo_2_r__resultado;

  sumador_completo sumador_completo_1 ();  // open: a, b, c, s__carreo, r__resultado
  sumador_completo sumador_completo_2 (.r__resultado(sumador_completo_2_r__resultado));  // open: a, b, c, s__carreo
  sumador_completo sumador_completo_3 ();  // open: a, b, c, s__carreo, r__resultado
  sumador_completo sumador_completo_4 (.a(sumador_completo_2_r__resultado));  // open: b, c, s__carreo, r__resultado
  sumador_completo sumador_completo_5 ();  // open: a, b, c, s__carreo, r__resultado
  sumador_completo sumador_completo_6 ();  // open: a, b, c, s__carreo, r__resultado
  sumador_completo sumador_completo_7 ();  // open: a, b, c, s__carreo, r__resultado
  sumador_completo sumador_completo_8 ();  // open: a, b, c, s__carreo, r__resultado
  sumador_completo Sumador_completo_de_dos_bits ();  // open: a, b, c, s__carreo, r__resultado
  sumador_completo sumador_completo_9 ();  // open: a, b, c, s__carreo, r__resultado
  sumador_completo sumador_completo_10 ();  // open: a, b, c, s__carreo, r__resultado
  sumador_completo sumador_completo_11 ();  // open: a, b, c, s__carreo, r__resultado

  // Notes on the sheet:
  //   carreo 
  //   carreo 
  //   resultado
endmodule

module sumador_completo (
  input  a,
  input  b,
  input  c,
  output s__carreo,
  output r__resultado
);

  wire a_b_c_out, a_b_c_prime_out, a_b_prime_c_out, a_b_prime_c_prime_out, a_prime_b_c_out,
       a_prime_b_c_prime_out, a_prime_b_prime_c_out, not_1_out, not_2_out, not_3_out;

  not not_1 (not_1_out, a);
  not not_2 (not_2_out, b);
  not not_3 (not_3_out, c);
  or a_b_c_prime (a_b_c_prime_out, a, b, not_3_out);
  or a_prime_b_c (a_prime_b_c_out, not_1_out, b, c);
  or a_b_prime_c (a_b_prime_c_out, a, not_2_out, c);
  or a_b_c (a_b_c_out, a, b, c);
  or a_prime_b_c_prime (a_prime_b_c_prime_out, not_1_out, b, not_3_out);
  or a_b_prime_c_prime (a_b_prime_c_prime_out, a, not_2_out, not_3_out);
  or a_prime_b_prime_c (a_prime_b_prime_c_out, not_1_out, not_2_out, c);
  and and_1 (s__carreo, a_b_c_prime_out, a_prime_b_c_out, a_b_prime_c_out, a_b_c_out);
  and and_2 (r__resultado, a_b_c_out, a_prime_b_c_prime_out, a_b_prime_c_prime_out, a_prime_b_prime_c_out);
endmodule
